// Digital circuit instruction_mem.dig as structural Verilog
module instruction_mem (
  input  [7:0] in_1,
  input  in_2,
  output [31:0] out_3
);

  ROM #(.AddrBits(8), .Bits(32)) rom_1 (.A(in_1), .sel(in_2), .D(out_3));

  // Notes on the sheet:
  //   contents of rom_1 (hex, n*v repeats v):
  //   4*61616161
endmodule
