// Digital circuit main.dig as structural Verilog
module main (
  input  Clock,
  output [5:0] FUNCT,
  output [5:0] out_3,
  output [31:0] out_4,
  output [31:0] out_5,
  output [3:0] out_6
);

  wire ALU_SRC, ex_mem_1_o_mr, ex_mem_1_o_mtr, ex_mem_1_o_mw, ex_mem_1_o_rw, id_ex_1_o_alus, id_ex_1_o_mtr,
       id_ex_1_o_mw, id_ex_1_o_rgd, id_ex_1_o_rw, id_ex_part_2_1_p9, MEM_TO_REG, mem_wb_1_o_mtr,
       mem_wb_1_o_rw, MR, RgD, RW, stall_1_p1, stall_1_p2, Write_MEM;
  wire [1:0] AO, FA, FB, id_ex_1_o_ao;
  wire [4:0] ex_mem_1_o_dest, id_ex_part_2_1_p6, id_ex_part_2_1_p8, mem_wb_1_o_dest, multiplexer_2_out,
       stall_1_p3;
  wire [7:0] control_1_mw;
  wire [31:0] _32x32_1_r_d1, _32x32_1_r_d2, add_1_s, bitextender_1_out, ex_mem_1_o_r2, ex_mem_1_o_result,
       id_ex_1_o_r1, id_ex_1_o_r2, id_ex_1_o_s32, mem_wb_1_o_alu_res, mem_wb_1_o_read_d, memory_24x32_1_data,
       multiplexer_3_out, multiplexer_4_out, multiplexer_5_out, pc_1_pc_out, R31, ula_1_resultado, WB;

  PC pc_1 (.Clok(Clock), .PC_IN(add_1_s), .PC_OUT(pc_1_pc_out));
  Add #(.Bits(32)) add_1 (.a(pc_1_pc_out), .b(32'h4), .c_i(1'b0), .s(add_1_s));  // open: c_o
  instruction_mem instruction_mem_1 (._32b__ADDR(pc_1_pc_out), ._1b__Enable(Clock), ._32b__Out(out_5));
  IF_ID if_id_1 (.In(out_5), .Clk(Clock), .Out({out_3, out_4[25:6], FUNCT}));
  Control control_1 (
    .RgD(control_1_mw[0]), .AluS(control_1_mw[1]), .MTR(control_1_mw[2]), .RW(control_1_mw[3]),
    .MR(control_1_mw[4]), .MW(control_1_mw[5]), .AO_1(control_1_mw[6]), .AO_0(control_1_mw[7]), .Clk(Clock),
    .Op(out_3));  // open: B, J, APC
  // Stall stall_1: pin names not known; wires that end beside it: stall_1_p1, stall_1_p2, stall_1_p3, out_4[25:21], out_4[20:16]
  Multiplexer #(.Bits(8)) multiplexer_1 (
    .sel(stall_1_p1), .in_0(control_1_mw), .in_1({8{1'b0}}),
    .out({AO, Write_MEM, MR, RW, MEM_TO_REG, ALU_SRC, RgD}));
  _32x32 _32x32_1 (
    ._32_W_d(WB), ._5__R_reg1(out_4[25:21]), ._5__R_reg2(out_4[20:16]), ._5b__A_set(mem_wb_1_o_dest),
    .Clk(Clock), ._1__W_e(mem_wb_1_o_rw), .R_d1(_32x32_1_r_d1), .R_d2(_32x32_1_r_d2), .R31(R31));
  BitExtender #(.inputBits(16), .outputBits(32)) bitextender_1 (.in({out_4[15:6], FUNCT}), .out(bitextender_1_out));
  ID_EX id_ex_1 (
    .RW(RW), .MR(MR), .MW(Write_MEM), .MTR(MEM_TO_REG), .RgD(RgD), .AluS(ALU_SRC), .AO(AO),
    .R_1(_32x32_1_r_d1), .R_2(_32x32_1_r_d2), .S_32(bitextender_1_out), .Clk(Clock), .O_RW(id_ex_1_o_rw),
    .O_MR(stall_1_p2), .O_MW(id_ex_1_o_mw), .O_MTR(id_ex_1_o_mtr), .O_RgD(id_ex_1_o_rgd),
    .O_AluS(id_ex_1_o_alus), .O_AO(id_ex_1_o_ao), .O_R1(id_ex_1_o_r1), .O_R2(id_ex_1_o_r2),
    .O_S32(id_ex_1_o_s32));
  // ID_EX_part_2 id_ex_part_2_1: pin names not known; wires that end beside it: Clock, out_4[25:21], out_4[20:16], out_4[15:11], FUNCT, id_ex_part_2_1_p6, stall_1_p3, id_ex_part_2_1_p8, id_ex_part_2_1_p9
  Multiplexer #(.Bits(5)) multiplexer_2 (
    .sel(id_ex_1_o_rgd), .in_0(stall_1_p3), .in_1(id_ex_part_2_1_p8), .out(multiplexer_2_out));
  Seven_Seg_Hex seven_seg_hex_1 (.d(R31[19:16]), .dp(1'b0));
  Seven_Seg_Hex seven_seg_hex_2 (.d(R31[15:12]), .dp(1'b0));
  Multiplexer #(.Selector_Bits(2), .Bits(32)) multiplexer_3 (
    .sel(FB), .in_0(id_ex_1_o_r2), .in_1(WB), .in_2(ex_mem_1_o_result), .in_3(ex_mem_1_o_result),
    .out(multiplexer_3_out));
  // ALU_Control alu_control_1: pin names not known; wires that end beside it: id_ex_1_o_ao[0], id_ex_1_o_ao[1], id_ex_part_2_1_p9, out_6
  Seven_Seg_Hex seven_seg_hex_3 (.d(R31[11:8]), .dp(1'b0));
  Multiplexer #(.Selector_Bits(2), .Bits(32)) multiplexer_4 (
    .sel(FA), .in_0(id_ex_1_o_r1), .in_1(WB), .in_2(ex_mem_1_o_result), .in_3(ex_mem_1_o_result),
    .out(multiplexer_4_out));
  Seven_Seg_Hex seven_seg_hex_4 (.d(R31[7:4]), .dp(1'b0));
  Seven_Seg_Hex seven_seg_hex_5 (.d(R31[3:0]), .dp(1'b0));
  Multiplexer #(.Bits(32)) multiplexer_5 (
    .sel(id_ex_1_o_alus), .in_0(multiplexer_3_out), .in_1(id_ex_1_o_s32), .out(multiplexer_5_out));
  forwarding_unit forwarding_unit_1 (
    .RS(id_ex_part_2_1_p6), .RT(stall_1_p3), .EX_MEM_dest(ex_mem_1_o_dest), .MEM_WB_dest(mem_wb_1_o_dest),
    .EX_MEM_rw(ex_mem_1_o_rw), .MEM_WB_rw(mem_wb_1_o_rw), .FA(FA), .FB(FB));
  ula ula_1 (
    .ALUControl(out_6), .A(multiplexer_4_out), .B(multiplexer_5_out), .Shamt({6{1'b0}}),
    .Resultado(ula_1_resultado));  // open: Zero
  EX_MEM ex_mem_1 (
    .RW(id_ex_1_o_rw), .MR(stall_1_p2), .MW(id_ex_1_o_mw), .MTR(id_ex_1_o_mtr), .Result(ula_1_resultado),
    .R_2(multiplexer_3_out), .Dest(multiplexer_2_out), .Clk(Clock), .O_RW(ex_mem_1_o_rw),
    .O_MR(ex_mem_1_o_mr), .O_MW(ex_mem_1_o_mw), .O_MTR(ex_mem_1_o_mtr), .O_Result(ex_mem_1_o_result),
    .O_R2(ex_mem_1_o_r2), .O_Dest(ex_mem_1_o_dest));
  memory_24x32 memory_24x32_1 (
    .address(ex_mem_1_o_result[23:0]), .write_data(ex_mem_1_o_r2), .mem_write(ex_mem_1_o_mw), .clock(Clock),
    .mem_read(ex_mem_1_o_mr), .data(memory_24x32_1_data));
  MEM_WB mem_wb_1 (
    .RW(ex_mem_1_o_rw), .MTR(ex_mem_1_o_mtr), .Read_D(memory_24x32_1_data), .Alu_res(ex_mem_1_o_result),
    .Dest(ex_mem_1_o_dest), .Clk(Clock), .O_RW(mem_wb_1_o_rw), .O_MTR(mem_wb_1_o_mtr),
    .O_Read_D(mem_wb_1_o_read_d), .O_Alu_res(mem_wb_1_o_alu_res), .O_Dest(mem_wb_1_o_dest));
  Multiplexer #(.Bits(32)) multiplexer_6 (
    .sel(mem_wb_1_o_mtr), .in_0(mem_wb_1_o_alu_res), .in_1(mem_wb_1_o_read_d), .out(WB));

  assign {out_4[31:26], out_4[5:0]} = {out_3, FUNCT};

  // Other names for the same wires on the sheet: AC[3:0] = out_6; OPCODE[5:0] = out_3

  // Notes on the sheet:
  //   Instruções na memória
  //   ADDI $S0, $S0, 5
  //   ADD $RA, $S0, $S0
  //   ADDI $RA, $RA, 5
  //   ADDI $RA, $RA, 5
  //   $S0 = 16, hex = 10
  //   $RA = 31, hex = 1F
  //   22100005
  //   0210f820
  //   23ff0005
  //   23ff0005
  //   Instrução [15-0]
  //   Instrução [20-16]
  //   Instrução [15-11]
  //   AluOP
endmodule
